# Fritzing sketch Synth-gauntlet_circuit (saved by Fritzing 1.0.5)
breadboards: 1

parts:
  Part1 = InvenSense MPU6050
  R1 = Basic Flex Resistor
  Part2 = Arduino Leonardo (Rev3b)
  R2 = Resistor [tolerance=±5% resistance=10k package="0402 [SMD]"]
  Part3 = 12 NeoPixel Ring [part_number=1643]
  Part4 = Adafruit AT42QT1010 Standalone Momentary Capacitive Touch Sensor [part_number="Adafruit #1374"]

nets:
  VDD: Part1.VCC, Part2.5V, R2.Pin_0, Part3.VDD, Part4.VDD
  GND: Part1.GND, R1.Pin_1, Part2.GND, Part3.GND, Part4.GND
  N1: Part1.SCL, Part2.SCL
  N2: Part1.SDA, Part2.SDA
  N3: R1.Pin_2, Part2.A0, R2.Pin_1
  N4: Part2.D6_PWM/A7, Part3.IN
  N5: Part2.D7, Part4.OUT

custom parts:
  12 NeoPixel Ring: 12 ultra bright smart LED NeoPixels are arranged in a circle with 1.5" (37mm) outer diameter. The rings are 'chainable' - connect the output pin of one to the input pin of another. Use only one microcontroller pin to control as many as you can chain together! Each LED is addressable as the driver chip is inside the LED. Each one has ~18mA constant current drive so the color will be very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
  Adafruit AT42QT1010 Standalone Momentary Capacitive Touch Sensor: This breakout board is the simplest way to create a project with a single "momentary" capacitive touch sensor. No microcontroller is required here - just power with 1.8 to 5.5VDC and touch the pad to activate the sensor. When a capacitive load is detected (e.g. a person touches the sensor-pad area) the red LED lights up and the output pin goes high. You can also solder a wire to the middle pad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
